# Fritzing sketch a3midifritzingboard (saved by Fritzing 0.9.3b)

parts:
  Teensy_3_1 = Teensy 3.1
  IC1 = IC, DIP package, 6 pins [chip_label=PC900V]
  U1 = MIDI_CONN_FEMALE [package=din_5_female]
  JP1 = RCA [package=rca_lock]
  R2 = Resistor [tolerance=±5% resistance=220 package=THT]
  C1 = Electrolytic Capacitor [capacitance=10µF voltage=35V package="100 mil [THT, electrolytic]"]
  U2 = MIDI_CONN_FEMALE [package=din_5_female]
  D1 = Diode [package=diode-1n4148]
  R3 = Resistor [tolerance=±5% resistance=220 package=THT]
  R1 = Resistor [tolerance=±5% resistance=220 package=THT]
  R4 = Resistor [tolerance=±5% resistance=220 package=THT]
  C2 = Tantalum Capacitor [capacitance=1μF package="100 mil [THT, tantalum]"]

nets:
  N1: Teensy_3_1.GND, IC1.pin5, U1.NC2, JP1.SHELL, C2.-
  N2: Teensy_3_1.D0, IC1.pin4, R4.Pin_0
  N3: Teensy_3_1.D1, R2.Pin_1
  N4: Teensy_3_1.A14/DAC, C1.+
  N5: Teensy_3_1.Vin, IC1.pin6, R1.Pin_0, R4.Pin_1, C2.+
  N6: IC1.pin1, D1.A, R3.Pin_1
  N7: IC1.pin2, U2.MIDI_OUT, D1.C
  N8: U1.MIDI_IN, R1.Pin_1
  N9: U1.MIDI_OUT, R2.Pin_0
  N10: JP1.PIN, C1.-
  N11: U2.MIDI_IN, R3.Pin_0

notes:
  midi out
  DAC out
  midi in
